# Fritzing sketch wiring (saved by Fritzing 0.9.3b)

parts:
  Bauteil1 = Arduino Pro Mini (3.3V)
  LED1 = LED - 3mm [color="Green (560nm)" package="3 mm [THT]"]
  R1 = Resistor [tolerance=±5% resistance=330 package=THT]
  Antenne_~8_3cm = CC1101 [part_number=CC1101]
  U1 = ESP32S-HiLetgo [part_number=ESP32S-HiLetgo]
  U2 = 2.4" TFT LCD screen, SPI, Touch-enabled

nets:
  VCC: Bauteil1.VCC, Antenne_~8_3cm.1, U1.3.3, U2.VCC
  GND: Bauteil1.GND, LED1.cathode, Antenne_~8_3cm.2, U1.GND, U2.GND
  N1: Bauteil1.SCK, Antenne_~8_3cm.4
  N2: Bauteil1.MISO, Antenne_~8_3cm.5
  N3: Bauteil1.MOSI, Antenne_~8_3cm.3
  N4: Bauteil1.D10, Antenne_~8_3cm.8
  N5: Bauteil1.D4, R1.Pin_0
  N6: Bauteil1.D2, Antenne_~8_3cm.7
  N7: Bauteil1.TXO, U1.GPIO16
  N8: LED1.anode, R1.Pin_1
  N9: U1.GPIO33, U2.LED
  N10: U1.GPIO25, U2.DC
  N11: U1.GPIO26, U2.RESET
  N12: U1.GPIO5, U2.CS
  N13: U1.GPIO18, U2.SCL
  N14: U1.GPIO19, U2.SDO
  N15: U1.GPIO23, U2.SDA

custom parts:
  ESP32S-HiLetgo: HiLetgo ESP-WROOM-32 ESP32 ESP-32S Development Board 2.4GHz Dual-Mode WiFi + Bluetooth Dual Cores Microcontroller The ESP32 integrated with Antenna switches, RF Balun, power amplifiers, low-noise amplifiers, filters, and management modules, and the entire solution occupies the least area of PCB. 2.4 GHz Wi-Fi plus Bluetooth dual-mode chip, with TSMC Ultra-low power consumption 40nm technology,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
  2.4" TFT LCD screen, SPI, Touch-enabled: 2.4", ILI9341-based TFT LCD screen with touch-sensing using the XPT2046 controller, SPI-compatible. There is also an SD-card version that is non-touch enabled but uses exactly the same board and pinout. This part is for both, though it should be noted that the SD reader and the touch screen are mutually incompatible
